// Logisim project Assignment1.circ as structural Verilog: 1 circuit, main circuit main
module main (
);

  wire and_3_out, and_4_out, and_5_out, and_6_out, and_7_out, demultiplexer_1_out0, demultiplexer_1_out1,
       demultiplexer_1_out2, demultiplexer_1_out3, demultiplexer_1_out4, demultiplexer_1_out5,
       demultiplexer_1_out6, demultiplexer_1_out7, demultiplexer_1_out8, not_1_out, not_2_out, not_3_out,
       not_4_out;
  wire [1:0] joystick_1_x, joystick_1_y;
  wire [3:0] and_1_out;

  // Probe on joystick_1_x
  Joystick #(.bits(2)) joystick_1 (.x(joystick_1_x), .y(joystick_1_y));
  // Probe on joystick_1_y
  // Probe on joystick_1_x
  // Probe on joystick_1_y
  not not_1 (not_1_out, joystick_1_x[0]);
  not not_2 (not_2_out, joystick_1_x[1]);
  not not_3 (not_3_out, joystick_1_y[0]);
  not not_4 (not_4_out, joystick_1_y[1]);
  and and_1 (and_1_out[0], joystick_1_x[0], joystick_1_y[0]);
  and and_2 (and_1_out[3], joystick_1_x[1], joystick_1_x[0], joystick_1_y[1], not_3_out);
  and and_3 (and_3_out, joystick_1_x[1], not_1_out, joystick_1_y[0]);
  and and_4 (and_4_out, not_2_out, joystick_1_x[0], not_4_out, joystick_1_y[0]);
  and and_5 (and_5_out, joystick_1_x[1], joystick_1_x[0], joystick_1_y[1], joystick_1_y[0]);
  and and_6 (and_6_out, not_2_out, joystick_1_x[0], joystick_1_y[1]);
  and and_7 (and_7_out, joystick_1_x[1], joystick_1_y[1], joystick_1_y[0]);
  or or_1 (and_1_out[1], and_3_out, and_4_out, and_5_out);
  or or_2 (and_1_out[2], and_6_out, and_7_out);
  Demultiplexer #(.select(4)) demultiplexer_1 (
    .out0(demultiplexer_1_out0), .out1(demultiplexer_1_out1), .out2(demultiplexer_1_out2),
    .out3(demultiplexer_1_out3), .out4(demultiplexer_1_out4), .out5(demultiplexer_1_out5),
    .out6(demultiplexer_1_out6), .out7(demultiplexer_1_out7), .out8(demultiplexer_1_out8), .in(1'b1),
    .sel(and_1_out));  // open: out9, out10, out11, out12, out13, out14, out15, en
  // Probe on and_1_out
  LED _3 (.in(demultiplexer_1_out3));
  LED _4 (.in(demultiplexer_1_out4));
  LED _5 (.in(demultiplexer_1_out5));
  LED _2 (.in(demultiplexer_1_out2));
  LED center (.in(demultiplexer_1_out0));
  LED _6 (.in(demultiplexer_1_out6));
  LED _1 (.in(demultiplexer_1_out1));
  LED _8 (.in(demultiplexer_1_out8));
  LED _7 (.in(demultiplexer_1_out7));

  // Notes on the sheet:
  //   Inputs x1, x2, x3, x4: 
  //   Outputs: y1, y2, y3, y4
  //   X2
  //   X1
  //   X4
  //   X3
  //   X'2
  //   X1'
  //   X'4
  //   X'3
  //   x1*x2'*x4
  //   x1'*x2*x3'*x4
  //   x1*x2*x3*x4
  //   x1'*x2*x3
  //   x1*x3*x4
  //   y1 = x1*x2*x3*x4'
  //   Y4 = x2*x4
  //   y2 = x1'*x2*x3 + x1*x3*x4
  //   Y3 = x1* x2'*x4 + x1'*x2*x3'*x4 + x1*x2*x3*x4
endmodule
