// Logisim project OLD as1-template.circ as structural Verilog: 2 circuits, main circuit main
module main (
);

  wire demultiplexer_1_out0, demultiplexer_1_out1, demultiplexer_1_out2, demultiplexer_1_out3,
       demultiplexer_1_out4, demultiplexer_1_out5, demultiplexer_1_out6, demultiplexer_1_out7,
       demultiplexer_1_out8;
  wire [1:0] joystick_1_x, joystick_1_y;
  wire [3:0] undriven;

  // Probe on joystick_1_x
  Joystick #(.bits(2)) joystick_1 (.x(joystick_1_x), .y(joystick_1_y));
  // Probe on joystick_1_y
  Demultiplexer #(.select(4)) demultiplexer_1 (
    .out0(demultiplexer_1_out0), .out1(demultiplexer_1_out1), .out2(demultiplexer_1_out2),
    .out3(demultiplexer_1_out3), .out4(demultiplexer_1_out4), .out5(demultiplexer_1_out5),
    .out6(demultiplexer_1_out6), .out7(demultiplexer_1_out7), .out8(demultiplexer_1_out8), .in(1'b1),
    .sel(undriven));  // open: out9, out10, out11, out12, out13, out14, out15, en
  // Probe on undriven
  LED _1 (.in(demultiplexer_1_out1));
  LED _4 (.in(demultiplexer_1_out4));
  LED _6 (.in(demultiplexer_1_out6));
  LED _2 (.in(demultiplexer_1_out2));
  LED center (.in(demultiplexer_1_out0));
  LED _7 (.in(demultiplexer_1_out7));
  LED _3 (.in(demultiplexer_1_out3));
  LED _5 (.in(demultiplexer_1_out5));
  LED _8 (.in(demultiplexer_1_out8));

  // Notes on the sheet:
  //   Joystick
  //   your circuit here
  //   verify your solution
endmodule

module \logic  (
  input  [1:0] x,
  input  [1:0] y,
  output [3:0] f
);

  wire nand_1_out, nand_2_out, nand_3_out, nand_4_out, nand_5_out, nand_6_out, nand_7_out, nand_8_out,
       nand_9_out, not_1_out, not_2_out, not_3_out, not_4_out;

  // Probe on x
  // Probe on y
  not not_1 (not_1_out, x[1]);
  not not_2 (not_2_out, x[0]);
  not not_3 (not_3_out, y[1]);
  not not_4 (not_4_out, y[0]);
  nand nand_1 (nand_1_out, x[0], not_3_out);
  nand nand_2 (nand_2_out, not_2_out, y[1], y[0]);
  nand nand_3 (nand_3_out, x[1], x[0], not_4_out);
  nand nand_4 (nand_4_out, x[1], not_3_out);
  nand nand_5 (nand_5_out, not_2_out, y[0]);
  nand nand_6 (nand_6_out, not_1_out, y[1], y[0]);
  nand nand_7 (nand_7_out, not_1_out, y[1]);
  nand nand_8 (nand_8_out, x[0], y[1], not_4_out);
  nand nand_9 (nand_9_out, not_2_out, y[1], y[0]);
  and and_1 (f[3], x[1], x[0], y[1], y[0]);
  nand nand_10 (f[0], nand_1_out, nand_2_out, nand_3_out);
  nand nand_11 (f[1], nand_4_out, nand_5_out, nand_6_out);
  nand nand_12 (f[2], nand_7_out, nand_8_out, nand_9_out);
endmodule
