// Logisim project Assignment2.circ as structural Verilog: 3 circuits, main circuit main
module main (
  output [3:0] out_1,
  output [2:0] out_2
);

  wire clear, clock_1_out, comparator_2_eq, comparator_3_eq, comparator_4_eq, latch1, latch2, latch3, match,
       not_1_out, not_2_out, not_3_out, not_4_out;
  wire [1:0] joystick_1_x, joystick_1_y;
  wire [3:0] logic1_1_f, register_1_q, register_2_q, register_3_q;

  Button Reset_Lock (.out(clear));
  logic1 logic1_1 (.x(joystick_1_x), .y(joystick_1_y), .f(logic1_1_f));
  Joystick #(.bits(2)) joystick_1 (.x(joystick_1_x), .y(joystick_1_y));
  // Probe on logic1_1_f
  Comparator #(.width(4)) comparator_1 (.a(logic1_1_f), .b(4'b0000), .eq(out_1[3]));  // open: gt, lt
  LED Green_open (.in(match));
  Register #(.width(4)) register_1 (.D(logic1_1_f), .Q(register_1_q), .clk(latch1), .clr(clear));  // open: en
  Clock clock_1 (.out(clock_1_out));
  Comparator #(.width(4)) comparator_2 (.a(4'b1000), .b(register_1_q), .eq(comparator_2_eq));  // open: gt, lt
  Register #(.width(4)) register_2 (.D(logic1_1_f), .Q(register_2_q), .clk(latch2), .clr(clear));  // open: en
  Comparator #(.width(4)) comparator_3 (.a(4'b0010), .b(register_2_q), .eq(comparator_3_eq));  // open: gt, lt
  Register #(.width(4)) register_3 (.D(logic1_1_f), .Q(register_3_q), .clk(latch3), .clr(clear));  // open: en
  D_Flip_Flop A1 (.clk(clock_1_out), .D(out_2[2]), .Q(out_1[2]), .reset(clear));  // open: Qn, preset, en
  D_Flip_Flop A2 (.clk(clock_1_out), .D(out_2[1]), .Q(out_1[1]), .reset(clear));  // open: Qn, preset, en
  D_Flip_Flop A3 (.clk(clock_1_out), .D(out_2[0]), .Q(out_1[0]), .reset(clear));  // open: Qn, preset, en
  Comparator #(.width(4)) comparator_4 (.a(4'b0111), .b(register_3_q), .eq(comparator_4_eq));  // open: gt, lt
  and u_match (match, comparator_4_eq, comparator_3_eq, comparator_2_eq);
  ROM #(.addrWidth(4), .dataWidth(3)) rom_1 (.addr(out_1), .data(out_2));  // open: sel
  and A1_2 (latch1, not_2_out, not_1_out, out_2[0]);
  not not_1 (not_1_out, out_2[1]);
  not not_2 (not_2_out, out_2[2]);
  and A2_2 (latch2, not_3_out, out_2[1], out_2[0]);
  not not_3 (not_3_out, out_2[2]);
  and A3_2 (latch3, out_2[2], not_4_out, out_2[0]);
  not not_4 (not_4_out, out_2[1]);

  // Other names for the same wires on the sheet: open = match; zero = out_1[3]; reset = clear

  // Notes on the sheet:
  //   operate the lock here
  //   is the lock open or closed?
  //   set combination here
  //   Direction(intput)
  //   A1 input
  //   A2 Input
  //   A3 Input
  //   contents of rom_1 (hex, n*v repeats v):
  //   1 1 3 3 5 5 0 0 0 2 2 4 4 6 7 7
  //   your circuit goes here
  //   A1 Output
  //   A2 Output
  //   A3 Output
  //   A1 Value
  //   A2 Value
  //   This makes it green light when open = match
  //   This is when reset button is clicked it clears the registers
  //   A3 Value
endmodule

// l0
module logic0 (
  input  [1:0] x,
  input  [1:0] y,
  output [3:0] f
);

  wire nand_1_out, nand_2_out, nand_3_out, nand_4_out, nand_5_out, nand_6_out, nand_7_out, nand_8_out,
       nand_9_out, not_1_out, not_2_out, not_3_out, not_4_out;

  // Probe on x
  // Probe on y
  not not_1 (not_1_out, x[1]);
  not not_2 (not_2_out, x[0]);
  not not_3 (not_3_out, y[1]);
  not not_4 (not_4_out, y[0]);
  nand nand_1 (nand_1_out, x[0], not_3_out);
  nand nand_2 (nand_2_out, not_2_out, y[1], y[0]);
  nand nand_3 (nand_3_out, x[1], x[0], not_4_out);
  nand nand_4 (nand_4_out, x[1], not_3_out);
  nand nand_5 (nand_5_out, not_2_out, y[0]);
  nand nand_6 (nand_6_out, not_1_out, y[1], y[0]);
  nand nand_7 (nand_7_out, not_1_out, y[1]);
  nand nand_8 (nand_8_out, x[0], y[1], not_4_out);
  nand nand_9 (nand_9_out, not_2_out, y[1], y[0]);
  and and_1 (f[3], x[1], x[0], y[1], y[0]);
  nand nand_10 (f[0], nand_1_out, nand_2_out, nand_3_out);
  nand nand_11 (f[1], nand_4_out, nand_5_out, nand_6_out);
  nand nand_12 (f[2], nand_7_out, nand_8_out, nand_9_out);
endmodule

// l1
module logic1 (
  input  [1:0] x,
  input  [1:0] y,
  output [3:0] f
);

  wire nand_1_out, nand_2_out, nand_3_out, nand_4_out, nand_5_out, not_1_out, not_2_out, not_3_out, not_4_out;

  // Probe on x
  // Probe on y
  not not_1 (not_1_out, x[1]);
  not not_2 (not_2_out, x[0]);
  not not_3 (not_3_out, y[1]);
  not not_4 (not_4_out, y[0]);
  nand nand_1 (nand_1_out, not_1_out, not_3_out);
  nand nand_2 (nand_2_out, x[1], y[1], y[0]);
  nand nand_3 (nand_3_out, not_2_out, y[0]);
  nand nand_4 (nand_4_out, y[1], y[0]);
  nand nand_5 (nand_5_out, not_1_out, y[1]);
  and and_1 (f[0], x[0], y[0]);
  nand nand_6 (f[1], nand_1_out, nand_2_out, nand_3_out);
  nand nand_7 (f[2], nand_4_out, nand_5_out);
  and and_2 (f[3], x[1], x[0], not_4_out);
endmodule
